# Fritzing sketch medidor_fuerza (saved by Fritzing 1.0.6)
circuit board: 9.24815cm x 7.66767cm
breadboards: 2

parts:
  M1 = DOIT Esp32 DevKit v1 (30 pins long, 11 pins width) [part_number=ESP32S-PIN30]
  A1 = Sparkfun load cell amplifier
  A3 = Sparkfun load cell amplifier
  LCD1 = 1_54in tft lcd
  S1 = Momentary Switch [package=ksa_sealed_tac_switch]
  LED2 = smd LED [color="Green (560nm)" package="1206 [SMD]"]
  LED1 = smd LED [color="Blue (470nm)" package="1206 [SMD]"]
  R2 = Resistor [tolerance=±5% resistance=220 package="2010 [SMD]"]
  R2_2 = Resistor [tolerance=±5% resistance=220 package="2010 [SMD]"]

nets:
  N1: M1.GND, A1.Pin_6, A3.Pin_6, LCD1.pin_1, LCD1.pin2, LCD1.pin_7, S1.3, LED2.cathode, LED1.cathode
  N2: M1.D4, R2.Pin_1
  N3: M1.D5, A1.Pin_7
  N4: M1.D19, A1.Pin_8
  N5: M1.D21, A3.Pin_8
  N6: M1.D22, A3.Pin_7
  N7: M1.D23, R2_2.Pin_1
  N8: M1.D32, S1.2
  N9: M1.D26, LCD1.pin_6
  N10: M1.D27, LCD1.pin_5
  N11: M1.D14, LCD1.pin3
  N12: M1.D13, LCD1.pin4
  N13: M1.VIN, A1.Pin_9, A1.Pin_10, A3.Pin_9, A3.Pin_10
  N14: LED2.anode, R2.Pin_0
  N15: LED1.anode, R2_2.Pin_0

notes:
  LOAD CELL #2
  5V CHARGER
  LOAD CELL #1

custom parts:
  DOIT Esp32 DevKit v1 (30 pins long, 11 pins width): The DOIT Esp32 DevKit v1 is one of the development board created by DOIT to evaluate the ESP-WROOM-32 module. It is based on the ESP32 microcontroller that boasts Wifi, Bluetooth, Ethernet and Low Power support all in a single chip. (vanepp) made breadboard work, adjusted pin numbering and labels and reduced size of schematic and cleaned up pcb. This chip is 30pins long (2 x15) and 11 pins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
  Sparkfun load cell amplifier: The SparkFun Load Cell Amplifier is a small breakout board for the HX711 IC that allows you to easily read load cells to measure weight.
  1_54in tft lcd: This is the DONGKER 1.54'' LCD Display Module, SPI 240x240 1.54'' LCD Display Module ST7789 Driver 240x240 3.3V IPS LCD Display Screen Module. The 1.54" display has 240x240 color pixels.
